// Logisim project cpu.circ as structural Verilog: 1 circuit, main circuit cpu
module cpu (
  input  clk,
  input  [31:0] Instruction,
  input  [31:0] MemReadData,
  output [31:0] MemAddress,
  output [31:0] ProgramCounter,
  output [31:0] ra,
  output [31:0] sp,
  output [31:0] t0,
  output [31:0] t1,
  output [31:0] t2,
  output [31:0] s0,
  output [31:0] s1,
  output [31:0] a0,
  output [3:0] MemWriteMask,
  output [31:0] MemWriteData
);

  wire ASel, BrEq, BrLt, BrUn, BSel, MemRW, partial_store_1_p1, partial_store_1_p3, partial_store_1_p4,
       PCsel, RegWEn;
  wire [1:0] WBSel;
  wire [2:0] ImmSel;
  wire [3:0] ALUSel;
  wire [31:0] adder_1_out, Immediate, rdVal, rs1Val;

  Register #(.width(32)) PC (.D(adder_1_out), .clk(clk), .Q(ProgramCounter));  // open: en, clr
  Adder #(.width(32)) adder_1 (.a(ProgramCounter), .b(32'h4), .out(adder_1_out));  // open: cin, cout
  imm_gen imm_gen_1 (.Instruction(Instruction), .Immediate(Immediate));  // open: ImmSel
  control_logic control_logic_1 (
    .Instruction(Instruction), .BrEq(BrEq), .BrLt(BrLt), .PCSel(PCsel), .RegWEn(RegWEn), .ImmSel(ImmSel),
    .BrUn(BrUn), .ASel(ASel), .BSel(BSel), .ALUSel(ALUSel), .MemRW(MemRW), .WBSel(WBSel));
  regfile regfile_1 (
    .ReadIndex1(Instruction[19:15]), .WriteIndex(Instruction[11:7]), .WriteData(rdVal), .RegWEn(1'b1),
    .clk(clk), .ra(ra), .sp(sp), .t0(t0), .t1(t1), .t2(t2), .s0(s0), .s1(s1), .a0(a0), .ReadData1(rs1Val));  // open: ReadIndex2, ReadData2
  // branch_comp branch_comp_1: pin names not known
  alu alu_1 (.A(rs1Val), .B(Immediate), .ALUSel(4'b0000), .ALUResult(rdVal));
  // partial_store partial_store_1: pin names not known; wires that end beside it: partial_store_1_p1, partial_store_1_p1, partial_store_1_p3, partial_store_1_p4, partial_store_1_p3
  // partial_load partial_load_1: pin names not known

  // Notes on the sheet:
  //   To IMEM
  //   IMEM (do **NOT** move this)
  //   From IMEM
  //   Inputs/Outputs for testing. Do **NOT** move these.
  //   It is OK to move the PC, RegFile, ALU, MEM, Branch Comp, Imm Gen, Partial Load, Partial Store and Control Logic to wherever is most convenient for you when constructing your CPU, and to delete this text
  //   To DMEM
  //   DMEM (do **NOT** move this)
  //   From DMEM
endmodule
